# Fritzing sketch sound_bar (saved by Fritzing 0.9.3b)
breadboards: 1

parts:
  Part1 = Arduino Nano (Rev3.0)
  Part2 = Breakout Board for Electret Microphone
  D1 = LED_BARGRAPH_10 [package=led_bargaph_10]
  R1 = Resistor [tolerance=±5% resistance=220 package="0805 [SMD]"]
  R2 = Resistor [tolerance=±5% resistance=220 package="0805 [SMD]"]
  R3 = Resistor [tolerance=±5% resistance=220 package="0805 [SMD]"]
  R4 = Resistor [tolerance=±5% resistance=220 package="0805 [SMD]"]
  R5 = Resistor [tolerance=±5% resistance=220 package="0805 [SMD]"]
  R6 = Resistor [tolerance=±5% resistance=220 package="0805 [SMD]"]
  R7 = Resistor [tolerance=±5% resistance=220 package="0805 [SMD]"]
  R8 = Resistor [tolerance=±5% resistance=220 package="0805 [SMD]"]
  R9 = Resistor [tolerance=±5% resistance=220 package="0805 [SMD]"]
  R10 = Resistor [tolerance=±5% resistance=220 package="0805 [SMD]"]
  U1 = LIPO-1000mAh [package=lipo-1000]

nets:
  N1: Part1.RESET, U1.+
  GND: Part1.GND, Part2.GND, D1.A_A, D1.B_A, D1.C_A, D1.D_A, D1.E_A, D1.F_A, D1.G_A, D1.H_A, D1.I_A, D1.J_A, U1.-
  N2: Part1.D2, R6.Pin_1
  N3: Part1.D3, R5.Pin_1
  N4: Part1.D4, R4.Pin_1
  N5: Part1.D5, R3.Pin_1
  N6: Part1.D6, R7.Pin_1
  N7: Part1.D7, R1.Pin_1
  N8: Part1.D8, R2.Pin_1
  N9: Part1.D9, R8.Pin_1
  N10: Part1.D10, R9.Pin_1
  N11: Part1.D11/MOSI, R10.Pin_1
  N12: Part1.A0, Part2.AUD
  N13: D1.J_C, R6.Pin_0
  N14: D1.I_C, R5.Pin_0
  N15: D1.H_C, R4.Pin_0
  N16: D1.G_C, R3.Pin_0
  N17: D1.F_C, R7.Pin_0
  N18: D1.E_C, R1.Pin_0
  N19: D1.D_C, R2.Pin_0
  N20: D1.C_C, R8.Pin_0
  N21: D1.B_C, R9.Pin_0
  N22: D1.A_C, R10.Pin_0
